# Fritzing sketch AlarmProtocol (saved by Fritzing 0.8.7b)
breadboards: 2

parts:
  Part1 = Arduino Mega 2560 (Rev3)
  DI1 = 7-Segment LED Display [package=THT]
  LED1 = LED - 5mm [color="Green (565nm)" package="5 mm [THT]"]
  LED2 = LED - 5mm [color="Yellow (595nm)" package="5 mm [THT]"]
  LED3 = LED - 5mm [color="Red (633nm)" package="5 mm [THT]"]
  S1 = Momentary Switch [package=ksa_sealed_tac_switch]
  J1 = Piezo Speaker
  R1 = Resistor [tolerance=±5% resistance=220 package=THT]
  R2 = Resistor [tolerance=±5% resistance=220 package=THT]
  R3 = Resistor [tolerance=±5% resistance=220 package=THT]
  R4 = Resistor [tolerance=±5% resistance=220 package=THT]
  R5 = Resistor [tolerance=±5% resistance=220 package=THT]
  R7 = Resistor [tolerance=±5% resistance=220 package=THT]
  R8 = Resistor [tolerance=±5% resistance=220 package=THT]
  R9 = Resistor [tolerance=±5% resistance=220 package=THT]
  R10 = Resistor [tolerance=±5% resistance=220 package=THT]
  R11 = Resistor [tolerance=±5% resistance=220 package=THT]
  R12 = Resistor [tolerance=±5% resistance=220 package=THT]
  R13 = Resistor [tolerance=±5% resistance=1k package=THT]  # not connected
  R14 = Resistor [tolerance=±5% resistance=220 package=THT]

nets:
  N1: Part1.D12_PWM, J1.pin2
  N2: Part1.D11_PWM, R1.Pin_1
  N3: Part1.D10_PWM, R2.Pin_1
  N4: Part1.D9_PWM, R3.Pin_1
  N5: Part1.D7_PWM, R4.Pin_1
  N6: Part1.D26, R9.Pin_0
  N7: Part1.D27, R10.Pin_0
  N8: Part1.D28, R14.Pin_0
  N9: Part1.D29, R8.Pin_1
  N10: Part1.D30, R7.Pin_1
  N11: Part1.D31, R11.Pin_1
  N12: Part1.D32, R12.Pin_1
  N13: Part1.D33, R5.Pin_0
  N14: DI1.cathodeE, R7.Pin_0
  N15: DI1.cathodeD, R8.Pin_0
  N16: DI1.cathodeC, R14.Pin_1
  N17: DI1.cathodeDP, R5.Pin_1
  N18: DI1.cathodeB, R10.Pin_1
  N19: DI1.cathodeA, R9.Pin_1
  N20: DI1.cathodeF, R11.Pin_0
  N21: DI1.cathodeG, R12.Pin_0
  N22: LED1.cathode, LED2.cathode, LED3.cathode, S1.4, J1.pin1, R4.Pin_0
  N23: LED1.anode, R1.Pin_0
  N24: LED2.anode, R2.Pin_0
  N25: LED3.anode, R3.Pin_0
